# Fritzing sketch RFID_Blynk_Sketch (saved by Fritzing 0.9.3b)
breadboards: 1

parts:
  U1 = NodeMCU V1.0
  Part1 = RFID-RC522-v2
  LED2 = LED - 5mm [color="Green (560nm)" package="5 mm [THT]"]
  LED3 = LED - 5mm [color="Blue (430nm)" package="5 mm [THT]"]
  SG1 = Buzzer 12mm [part_number=COM-07950 package=buzzer-12mm-ns]
  U2 = 2-Channel 5v Relay Shield [package=relay-2ch5v10a]

nets:
  N1: U1.D0, U2.IN1
  N2: U1.D1, LED2.cathode
  N3: U1.D2, LED3.cathode
  N4: U1.D3, SG1.1
  N5: U1.D4, Part1.RST
  3V3: U1.3V3, Part1.3.3V, LED2.anode, LED3.anode, U2.VCC
  GND: U1.GND, Part1.GND, SG1.2, U2.GND
  N6: U1.D5, Part1.SCK
  N7: U1.D6, Part1.MISO
  N8: U1.D7, Part1.MOSI
  N9: U1.D8, Part1.SDA
  N10: U2.K1-On, U2.K2-In

custom parts:
  NodeMCU V1.0: ESP8266 based NodeMCU
  RFID-RC522-v2: A simple China made RFID-RC522 Reader; do check the pin labels, as this is a MFRC522 based clone.
  Buzzer 12mm: Buzzer 12mm Spark Fun Electronics SKU : Comp-Buzzer Through hole This is a small 12mm round speaker that operates around the audible 2kHz range. You can use these speakers to create simple music or user interfaces. This is not a true piezoelectric speaker but behaves similarly. Instead of a piezoelectric crystal that vibrates with an electric current, this tiny speaker uses an electromagnet to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
  2-Channel 5v Relay Shield: 2 Channel 5v Relay Shield w. 2x SPD-06VDC-SD-C
